# Fritzing sketch wiring-diagram (saved by Fritzing 0.9.2b)
breadboards: 2

parts:
  Parte1 = Motor Driver 1A Dual TB6612FNG  # not connected
  Parte2 = Motor Driver 1A Dual TB6612FNG  # not connected
  U1 = LM2596 step down module
  Parte3 = Arduino Mega 2560 (Rev3)
  M1 = damikro tbs mini
  Parte4 = Motor Driver 1A Dual TB6612FNG  # not connected
  SP1 = SPEAKER [package=pcb_mount_speaker]
  M2 = ps2 gamepad [package=THT]

nets:
  GND: U1.IN-, U1.OUT-, Parte3.GND, M1.SP-GND, M1.Prop1_input_gnd, M1.Out_3+4_gnd, M1.Prog_GND, M2.GND
  N1: U1.OUT+, M1.Prop1_input_pwr, M1.Out_1+2_pwr
  N2: Parte3.A0, M2.ATT
  N3: Parte3.A1, M2.CMD
  N4: Parte3.A2, M2.DAT
  N5: Parte3.A3, M2.CLK
  3V3: Parte3.3V3, M2.3.3V, M2.SHLD
  N6: Parte3.D49, M1.Prop1_input_sig, M1.Prop1_output_sig
  N7: Parte3.D51, M1.Prop2_input_sig
  N8: Parte3.D53, M1.Prop3_input_sig
  N9: M1.SP+, SP1.-
  N10: M1.SP-, SP1.+

notes:
  14,6V Battery (to 7,2V)
  [smoke generator, smoke fan], [left motor, right motor], [gun elevation, turret rotation]

custom parts:
  LM2596 step down module: LM2596 DC-DC step down power supply module 3 A.
  damikro tbs mini: damikro tbs mini digital multifunctional RC sound unit. Pcb view has been omitted as not useful.
  ps2 gamepad: PS2 gamepad. Warning! PCB view is designed for the female connector available from https://www.robotshop.com/en/ps2-connector.html. However there is no mechanical information that I can find so ipcb was generated from a scaled jpg and may well be wrong. Print the footprint out and check it against a real part before ordering boards!
